// Logisim project p1_ej3.circ as structural Verilog: 3 circuits, main circuit NAND_AND
module NAND_AND (
  input  p,
  input  q,
  output pANDq
);

  wire nand_1_out;

  nand nand_1 (nand_1_out, p, q);
  nand nand_2 (pANDq, nand_1_out, nand_1_out);
endmodule

module NAND_NOT (
  input  p,
  output NOTp
);

  nand nand_1 (NOTp, p, p);
endmodule

module NAND_OR (
  input  p,
  input  q,
  output pORq
);

  wire nand_1_out, nand_2_out;

  nand nand_1 (nand_1_out, p, p);
  nand nand_2 (nand_2_out, q, q);
  nand nand_3 (pORq, nand_1_out, nand_2_out);
endmodule
